# Fritzing sketch Load Cell to Raspberry Pi (saved by Fritzing 0.9.3b)

parts:
  Raspberry_Pi_1 = Raspberry Pi 3 [part_number=RPI-3-V1.2]
  Part2 = HX711 Weighing Sensor Module
  Load_Cell1 = Load Cell - Red/white/black/green

nets:
  N1: Raspberry_Pi_1.GIPO5, Part2.DO/RX
  N2: Raspberry_Pi_1.GIPO6, Part2.CK/TX
  GND: Raspberry_Pi_1.GND, Part2.GND
  5V: Raspberry_Pi_1.5V, Part2.VCC
  N3: Part2.E+, Load_Cell1.wire1
  N4: Part2.E-, Load_Cell1.wire3
  N5: Part2.A+, Load_Cell1.wire4
  N6: Part2.A-, Load_Cell1.wire2

custom parts:
  Load Cell - Red/white/black/green: A rectangle load cell/weighting pressure Sensor with four wires - Red, white, black, green. Normally corresponding with E+, E-, A+, A- respectively.
